# Fritzing sketch Assignment 1 wire diagram (saved by Fritzing 0.9.3b)
breadboards: 1

parts:
  U1 = ESP32S-HiLetgo [part_number=ESP32S-HiLetgo]
  DHT1 = DHT22 Humidity and Temperature Sensor  # not connected
  Grove1 = Grove OLED 128x96  # not connected
  R1 = Resistor [tolerance=±5% resistance=220k package="1206 [SMD]"]
  R2 = Resistor [tolerance=±5% resistance=220k package="1206 [SMD]"]
  R3 = Resistor [tolerance=±5% resistance=220k package="1206 [SMD]"]
  R4 = Resistor [tolerance=±5% resistance=220k package="1206 [SMD]"]
  R5 = Resistor [tolerance=±5% resistance=1000 package="1206 [SMD]"]
  LED1 = LED - 5mm [color="Red (633nm)" current=0.030 package="5 mm [THT]"]
  R6 = Resistor [tolerance=±5% resistance=1000 package="1206 [SMD]"]
  LED2 = LED - 5mm [color="Red (633nm)" current=0.030 package="5 mm [THT]"]
  J1 = Piezo Speaker
  R8 = Resistor [tolerance=±5% resistance=1000 package="1206 [SMD]"]
  S4 = Pushbutton [package="[THT]"]
  S3 = Pushbutton [package="[THT]"]
  S2 = Pushbutton [package="[THT]"]
  S1 = Pushbutton [package="[THT]"]

nets:
  N1: U1.3.3, R1.Pin_0, R2.Pin_0, R3.Pin_0, R4.Pin_0
  N2: U1.GND, R5.Pin_1, R6.Pin_1, R8.Pin_1, S4.Pin_1, S4.Pin_2, S3.Pin_1, S3.Pin_2, S2.Pin_1, S2.Pin_2, S1.Pin_1, S1.Pin_2
  N3: U1.GPIO11, J1.pin2
  N4: U1.GPIO6, R1.Pin_1, S1.Pin_3, S1.Pin_4
  N5: U1.GPIO7, R2.Pin_1, S2.Pin_3, S2.Pin_4
  N6: U1.GPIO8, R3.Pin_1, S3.Pin_3, S3.Pin_4
  N7: U1.GPIO15, R4.Pin_1, S4.Pin_3, S4.Pin_4
  N8: U1.GPIO2, R6.Pin_0, LED2.cathode, LED2.anode
  N9: U1.GPIO0, LED1.anode
  N10: R5.Pin_0, LED1.cathode
  N11: J1.pin1, R8.Pin_0

custom parts:
  ESP32S-HiLetgo: HiLetgo ESP-WROOM-32 ESP32 ESP-32S Development Board 2.4GHz Dual-Mode WiFi + Bluetooth Dual Cores Microcontroller The ESP32 integrated with Antenna switches, RF Balun, power amplifiers, low-noise amplifiers, filters, and management modules, and the entire solution occupies the least area of PCB. 2.4 GHz Wi-Fi plus Bluetooth dual-mode chip, with TSMC Ultra-low power consumption 40nm technology,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
